// Logisim project M4_8.1.circ as structural Verilog: 1 circuit, main circuit main
module main (
);

  wire ABUSHL, ABUSPC, ABUSSP, ABUST, ALUEN, and_1_out, and_3_out, and_4_out, and_9_out, and_10_out,
       and_11_out, C, CLK, CNST1, CNSTFF, comparator_1_eq, comparator_2_eq, COUT, D0, d_ff_1_q, d_ff_2_qn,
       d_ff_4_qn, DBUSA, DBUSALU, DBUSB, DBUSCNST, DBUSH, DBUSL, DBUSPCH, DBUSPCL, DBUSS, DBUSSPH, DBUSSPL,
       DBUSTL, demultiplexer_1_out1, DREAD, DWRITE, HALT, LOADA, LOADB, LOADC, LOADH, LOADL, LOADPC, LOADSPH,
       LOADSPL, LOADTH, LOADTL, LOADZ, multiplexer_2_out, multiplexer_3_out, multiplexer_4_out, nor_1_out,
       nor_2_out, not_1_out, not_3_out, not_4_out, not_5_out, nPOR, NXTI, OP0, or_1_out, or_2_out, or_3_out,
       or_5_out, or_8_out, or_9_out, PCINC, PH0, por_1_out, RAMREAD, RAMWRITE, RAWCLK, RST, RUN, RUNNING,
       s_r_ff_1_q, s_r_ff_2_q, SPL_carry, SPOP, SPUP, SSI, SSP, SSS, STOP, undriven, Z, ZOUT;
  wire [0:0] ALUL_data, or_10_out;
  wire [2:0] ALUOP, PH;
  wire [3:0] ALUH_data, ALUL_data_2, bit_extender_2_out;
  wire [7:0] A, B, BOOTROM_data, controlled_buffer_7_out, H_q, IR, L_q, register_1_q, TL;
  wire [7:1] DATA;
  wire [15:0] AD, PC, SP;
  wire [15:8] PCDATA16;
  wire [23:0] bit_extender_1_out, IDECODE_data;
  wire [23:3] and_8_out;

  D_Flip_Flop #(.trigger("falling")) d_ff_1 (.D(PH0), .clk(RAWCLK), .Q(d_ff_1_q));  // open: Qn, preset, reset
  S_R_Flip_Flop s_r_ff_1 (.S(SSI), .R(SSS), .clk(RAWCLK), .Q(s_r_ff_1_q));  // open: reset, Qn, preset
  Clock clock_1 (.out(RAWCLK));
  D_Flip_Flop d_ff_2 (.D(d_ff_1_q), .clk(RAWCLK), .Qn(d_ff_2_qn));  // open: Q, preset, reset
  or or_1 (or_1_out, SSI, RUN);
  or or_2 (or_2_out, RST, STOP, HALT, SSS);
  POR #(.PorHighDuration(1), .porsize(1)) por_1 (.out(por_1_out));
  and and_1 (and_1_out, RAWCLK, nPOR);
  S_R_Flip_Flop #(.trigger("low")) s_r_ff_2 (
    .S(or_1_out), .R(or_2_out), .clk(1'b0), .Q(s_r_ff_2_q), .reset(RST));  // open: Qn, preset
  and and_2 (SSS, d_ff_1_q, d_ff_2_qn, s_r_ff_1_q);
  Counter #(.max('hffff), .width(16)) u_PC (
    .clr(RST), .load(LOADPC), .count(or_3_out), .clk(CLK), .D({PCDATA16, DATA, D0}), .Q(PC));  // open: up, carry
  or or_3 (or_3_out, PH0, PCINC);
  Counter SPL (
    .clr(RST), .load(LOADSPL), .up(SPUP), .count(SPOP), .clk(CLK), .D({DATA, D0}), .carry(SPL_carry),
    .Q(SP[7:0]));
  not not_1 (not_1_out, por_1_out);
  Multiplexer multiplexer_1 (.in0(SSP), .in1(and_1_out), .out(CLK), .sel(RUNNING));
  D_Flip_Flop d_ff_3 (.D(s_r_ff_2_q), .clk(RAWCLK), .Q(RUNNING));  // open: Qn, preset, reset
  nor nor_1 (nor_1_out, AD[15], AD[14], AD[13], AD[12], AD[11], AD[10]);
  ROM #(.addrWidth(10)) BOOTROM (.addr(AD[9:0]), .data(BOOTROM_data));
  D_Flip_Flop #(.trigger("falling")) d_ff_4 (.D(not_1_out), .clk(RAWCLK), .Qn(d_ff_4_qn));  // open: Q, preset, reset
  or or_4 (RST, por_1_out, d_ff_4_qn);
  Counter #(.max('h7), .width(3)) PHASECOUNTER (
    .clr(RST), .load(NXTI), .clk(CLK), .D(3'b000), .Q(PH));  // open: up, count, carry
  assign {DATA, D0} = DBUSPCL ? PC[7:0] : 8'bz;  // Controlled_Buffer controlled_buffer_1
  assign {DATA, D0} = DBUSPCH ? PC[15:8] : 8'bz;  // Controlled_Buffer controlled_buffer_2
  assign AD = or_5_out ? PC : 16'bz;  // Controlled_Buffer controlled_buffer_3
  or or_5 (or_5_out, PH0, ABUSPC);
  and and_3 (and_3_out, SPOP, SPL_carry);
  and and_4 (and_4_out, nor_1_out, DREAD);
  not not_2 (nPOR, RST);
  Counter counter_1 (
    .clr(RST), .load(LOADSPH), .up(SPUP), .count(and_3_out), .clk(CLK), .D({DATA, D0}), .Q(SP[15:8]));  // open: carry
  assign {DATA, D0} = and_4_out ? BOOTROM_data : 8'bz;  // Controlled_Buffer controlled_buffer_4
  nor nor_2 (nor_2_out, PH[0], PH[1], PH[2]);
  ROM #(.addrWidth(11), .dataWidth(24)) IDECODE (.addr({IR, PH}), .data(IDECODE_data));
  LED led_1 (.in(RUNNING));
  and and_5 (PH0, nPOR, nor_2_out);
  assign AD = ABUSSP ? SP : 16'bz;  // Controlled_Buffer controlled_buffer_5
  RAM #(.addrWidth(10), .asyncread("true"), .databus("bidir"), .\type ("nonvolatile")) ram_1 (
    .addr(AD[9:0]), .we(RAMWRITE), .oe(RAMREAD), .clk(CLK));  // open: data
  LED led_2 (.in(RST));
  Button button_1 (.out(RUN));
  Comparator #(.width(6)) comparator_1 (.a({6{1'b1}}), .b(AD[15:10]), .eq(comparator_1_eq));  // open: gt, lt
  LED led_3 (.in(CLK));
  Hex_Digit_Display hex_digit_display_1 (.value(PC[15:12]));  // open: dp
  Button button_2 (.out(STOP));
  assign bit_extender_1_out = {{23{PH0}}, PH0};  // Bit_Extender bit_extender_1
  and and_6 (RAMREAD, DREAD, comparator_1_eq);
  and and_7 (RAMWRITE, comparator_1_eq, DWRITE);
  Hex_Digit_Display hex_digit_display_2 (.value(PC[11:8]));  // open: dp
  Hex_Digit_Display hex_digit_display_3 (.value(PC[7:4]));  // open: dp
  assign {and_8_out[23:18], ALUEN, SPUP, SPOP, OP0, PCINC, and_8_out[12:3], ALUOP} = IDECODE_data & ~bit_extender_1_out;  // AND_Gate and_8, 24 bits wide
  Hex_Digit_Display hex_digit_display_4 (.value(PC[3:0]));  // open: dp
  Hex_Digit_Display hex_digit_display_5 (.value(IR[7:4]));  // open: dp
  Button button_3 (.out(SSP));
  Button button_4 (.out(SSI));
  Register u_IR (.D({DATA, D0}), .en(PH0), .clk(CLK), .Q(IR), .clr(undriven));
  assign {DATA, D0} = RAMREAD ? controlled_buffer_7_out : 8'bz;  // Controlled_Buffer controlled_buffer_6
  assign controlled_buffer_7_out = RAMWRITE ? {DATA, D0} : 8'bz;  // Controlled_Buffer controlled_buffer_7
  Hex_Digit_Display hex_digit_display_6 (.value(IR[3:0]));  // open: dp
  not not_3 (not_3_out, Z);
  not not_4 (not_4_out, C);
  Hex_Digit_Display hex_digit_display_7 (.value(bit_extender_2_out));  // open: dp
  assign bit_extender_2_out = {{1{1'b0}}, PH};  // Bit_Extender bit_extender_2
  Multiplexer #(.select(3)) multiplexer_2 (
    .in0(Z), .in1(not_3_out), .in2(C), .in3(not_4_out), .out(multiplexer_2_out), .sel(ALUOP));  // open: in4, in5, in6, in7
  and and_9 (and_9_out, multiplexer_2_out, and_8_out[11]);
  Hex_Digit_Display hex_digit_display_8 (.value(DATA[7:4]));  // open: dp
  Hex_Digit_Display hex_digit_display_9 (.value({DATA[3:1], D0}));  // open: dp
  or or_6 (NXTI, and_9_out, and_8_out[12]);
  Register u_A (.D({DATA, D0}), .en(LOADA), .clk(CLK), .Q(A));  // open: clr
  Register u_B (.D({DATA, D0}), .en(LOADB), .clk(CLK), .Q(B));  // open: clr
  Register H (.D({DATA, D0}), .en(LOADH), .clk(CLK), .Q(H_q));  // open: clr
  Register L (.D({DATA, D0}), .en(LOADL), .clk(CLK), .Q(L_q));  // open: clr
  Register u_TL (.D({DATA, D0}), .en(LOADTL), .clk(CLK), .Q(TL));  // open: clr
  Register TH (.D({DATA, D0}), .en(LOADTH), .clk(CLK), .Q(PCDATA16));  // open: clr
  not not_5 (not_5_out, PH0);
  Demultiplexer #(.select(4)) demultiplexer_1 (
    .out1(demultiplexer_1_out1), .out2(DBUSPCH), .out3(DBUSPCL), .out4(DBUSSPH), .out5(DBUSSPL),
    .out6(DBUSTL), .out7(DBUSA), .out8(DBUSB), .out9(DBUSH), .out10(DBUSL), .out11(DBUSS), .out12(DBUSALU),
    .out13(DBUSCNST), .in(not_5_out), .sel(and_8_out[10:7]));  // open: out0, out14, out15
  assign {DATA, D0} = DBUSA ? A : 8'bz;  // Controlled_Buffer controlled_buffer_8
  assign {DATA, D0} = DBUSB ? B : 8'bz;  // Controlled_Buffer controlled_buffer_9
  and and_10 (and_10_out, OP0, not_5_out);
  Demultiplexer #(.select(3)) demultiplexer_2 (
    .out1(ABUSPC), .out2(ABUSSP), .out3(ABUSHL), .out4(ABUST), .out5(HALT), .out6(CNST1), .out7(CNSTFF),
    .in(and_10_out), .sel(ALUOP));  // open: out0
  assign {DATA, D0} = DBUSH ? H_q : 8'bz;  // Controlled_Buffer controlled_buffer_10
  assign AD = ABUSHL ? {H_q, L_q} : 16'bz;  // Controlled_Buffer controlled_buffer_11
  assign {DATA, D0} = DBUSL ? L_q : 8'bz;  // Controlled_Buffer controlled_buffer_12
  assign {DATA, D0} = DBUSTL ? TL : 8'bz;  // Controlled_Buffer controlled_buffer_13
  assign AD = ABUST ? {PCDATA16, TL} : 16'bz;  // Controlled_Buffer controlled_buffer_14
  TTY tty_1 (.data({DATA[6:1], D0}), .clk(CLK), .we(and_11_out));  // open: clr
  or or_7 (DREAD, PH0, demultiplexer_1_out1);
  Demultiplexer #(.select(4)) demultiplexer_3 (
    .out1(DWRITE), .out2(LOADPC), .out3(LOADSPH), .out4(LOADSPL), .out5(LOADTH), .out6(LOADTL), .out7(LOADA),
    .out8(LOADB), .out9(LOADH), .out10(LOADL), .out11(LOADC), .out12(LOADZ), .in(not_5_out),
    .sel(and_8_out[6:3]));  // open: out0, out13, out14, out15
  Multiplexer multiplexer_3 (.in0(D0), .in1(COUT), .out(multiplexer_3_out), .sel(ALUEN));
  or or_8 (or_8_out, ALUEN, LOADC);
  Register #(.width(1)) u_C (.D(multiplexer_3_out), .en(or_8_out), .clk(CLK), .Q(C));  // open: clr
  and and_11 (and_11_out, comparator_2_eq, DWRITE);
  Comparator #(.width(16)) comparator_2 (.a(16'h400), .b(AD), .eq(comparator_2_eq));  // open: gt, lt
  ROM #(.addrWidth(12), .dataWidth(5)) ALUL (.addr({ALUOP, TL[3:0], A[3:0], C}), .data({ALUL_data[0], ALUL_data_2}));
  ROM #(.addrWidth(12), .dataWidth(5)) ALUH (.addr({ALUOP, TL[7:4], A[7:4], ALUL_data[0]}), .data({COUT, ALUH_data}));
  assign {DATA, D0} = DBUSS ? {{6{1'b0}}, C, Z} : 8'bz;  // Controlled_Buffer controlled_buffer_15
  Multiplexer multiplexer_4 (.in0(D0), .in1(ZOUT), .out(multiplexer_4_out), .sel(ALUEN));
  or or_9 (or_9_out, ALUEN, LOADZ);
  assign {DATA, D0} = DBUSCNST ? {{7{CNSTFF}}, or_10_out[0]} : 8'bz;  // Controlled_Buffer controlled_buffer_16
  or or_10 (or_10_out[0], CNSTFF, CNST1);
  Register #(.width(1)) u_Z (.D(multiplexer_4_out), .en(or_9_out), .clk(CLK), .Q(Z));  // open: clr
  nor nor_3 (ZOUT, ALUH_data[3], ALUH_data[2], ALUH_data[1], ALUH_data[0], ALUL_data_2[3], ALUL_data_2[2], ALUL_data_2[1], ALUL_data_2[0]);
  Register #(.trigger("falling")) register_1 (
    .D({ALUH_data, ALUL_data_2}), .en(ALUEN), .clk(CLK), .Q(register_1_q));  // open: clr
  assign {DATA, D0} = DBUSALU ? register_1_q : 8'bz;  // Controlled_Buffer controlled_buffer_17

  // Other names for the same wires on the sheet: DATA[0] = D0; PCDATA16[7:0] = {DATA, D0}

  // Notes on the sheet:
  //   contents of BOOTROM (hex, n*v repeats v):
  //   20 ff ff 8 53 10 4 0 8 65 10 4 0 8 6c 10 4 0 8 66 10 4 0 8 74 10 4 0 8 65 10 4 0 8 73 10 4 0 8 74 10
  //   4 0 8 a 10 4 0 8 4a 10 4 0 8 4d 10 4 0 8 50 10 4 0 8 20 10 4 0 80 0 57 8 4e 10 4 0 8 4f 10 4 0 8 4b
  //   10 4 0 ff 8 4f 10 4 0 8 4b 10 4 0 8 a 10 4 0 8 4a 10 4 0 8 53 10 4 0 8 52 10 4 0 8 20 10 4 0 81 0 8f
  //   8 4f 10 4 0 8 4b 10 4 0 8 a 10 4 0 80 0 b3 8 4f 10 4 0 8 4b 10 4 0 8 a 10 4 0 8 52 10 4 0 8 45 10 4
  //   0 8 54 10 4 0 8 20 10 4 0 82 21 0 d5 81 0 bd ff 80 0 0 4 61 83 0 d4 10 4 0 5d 56 65 1 51 86 0 bd 59
  //   65 0 52 80 0 bd 82 41 6c 6c 20 74 65 73 74 73 20 70 61 73 73 65 64 a
  //   contents of IDECODE (hex, n*v repeats v):
  //   0 60a9 60b1 50bc 5*0 60a9 60b1 50c4 5*0 60a9 60b1 50cc 5*0 60a9 60b1 50d4 5*0 50bb 7*0 50c3 23*0
  //   70b9 7*0 70c1 7*0 70c9 7*0 70d1 39*0 60a9 60b1 538c 5*0 60a9 60b1 540c 5*0 60a9 60b1 548c 5*0 60a9
  //   60b1 550c 5*0 538b 7*0 540b 87*0 6099 70a1 6*0 60c9 70d1 374*0 13c0 7*0 13d0 7*0 13c8 7*0 1438 7*0
  //   1450 7*0 1448 7*0 1538 7*0 1540 7*0 1548 7*0 14b8 7*0 14c0 7*0 14d0 7*0 430 3c0 1338 5*0 16d8 7*0
  //   56de 7*0 16e0 7*0 56e6 7*0 6b0 21001 6*0 430 21001 6*0 60b1 21001 6*0 430 21638 6*0 60b1 21638 6*0
  //   430 21639 6*0 60b1 21639 6*0 430 2163a 6*0 60b1 2163a 6*0 430 2163b 6*0 60b1 2163b 6*0 430 2163c 6*0
  //   60b1 2163c 6*0 2163d 7*0 2163e 7*0 2163f 127*0 60a9 5091 6*0 60a9 60b1 c10a c18a 1310 0 0 0 18000
  //   1c0b2 40aa 1310 4*0 60a9 60b1 801 1310 4*0 60a9 60b1 800 1310 4*0 60a9 60b1 803 1310 4*0 60a9 60b1
  //   802 1310 956*0 1000 7*0 5005
  //   RUN
  //   RST
  //   CLK
  //   PC
  //   NXTIC
  //   IR
  //   NXTI
  //   PH
  //   contents of ALUL (hex, n*v repeats v):
  //   0 1 1 2 2 3 3 4 4 5 5 6 6 7 7 8 8 9 9 a a b b c c d d e e f f 10 1 2 2 3 3 4 4 5 5 6 6 7 7 8 8 9 9 a
  //   a b b c c d d e e f f 10 10 11 2 3 3 4 4 5 5 6 6 7 7 8 8 9 9 a a b b c c d d e e f f 10 10 11 11 12
  //   3 4 4 5 5 6 6 7 7 8 8 9 9 a a b b c c d d e e f f 10 10 11 11 12 12 13 4 5 5 6 6 7 7 8 8 9 9 a a b b
  //   c c d d e e f f 10 10 11 11 12 12 13 13 14 5 6 6 7 7 8 8 9 9 a a b b c c d d e e f f 10 10 11 11 12
  //   12 13 13 14 14 15 6 7 7 8 8 9 9 a a b b c c d d e e f f 10 10 11 11 12 12 13 13 14 14 15 15 16 7 8 8
  //   9 9 a a b b c c d d e e f f 10 10 11 11 12 12 13 13 14 14 15 15 16 16 17 8 9 9 a a b b c c d d e e f
  //   f 10 10 11 11 12 12 13 13 14 14 15 15 16 16 17 17 18 9 a a b b c c d d e e f f 10 10 11 11 12 12 13
  //   13 14 14 15 15 16 16 17 17 18 18 19 a b b c c d d e e f f 10 10 11 11 12 12 13 13 14 14 15 15 16 16
  //   17 17 18 18 19 19 1a b c c d d e e f f 10 10 11 11 12 12 13 13 14 14 15 15 16 16 17 17 18 18 19 19
  //   1a 1a 1b c d d e e f f 10 10 11 11 12 12 13 13 14 14 15 15 16 16 17 17 18 18 19 19 1a 1a 1b 1b 1c d
  //   e e f f 10 10 11 11 12 12 13 13 14 14 15 15 16 16 17 17 18 18 19 19 1a 1a 1b 1b 1c 1c 1d e f f 10 10
  //   11 11 12 12 13 13 14 14 15 15 16 16 17 17 18 18 19 19 1a 1a 1b 1b 1c 1c 1d 1d 1e f 10 10 11 11 12 12
  //   13 13 14 14 15 15 16 16 17 17 18 18 19 19 1a 1a 1b 1b 1c 1c 1d 1d 1e 1e 1f 0 1f 1 0 2 1 3 2 4 3 5 4
  //   6 5 7 6 8 7 9 8 a 9 b a c b d c e d f e 1f 1e 0 1f 1 0 2 1 3 2 4 3 5 4 6 5 7 6 8 7 9 8 a 9 b a c b d
  //   c e d 1e 1d 1f 1e 0 1f 1 0 2 1 3 2 4 3 5 4 6 5 7 6 8 7 9 8 a 9 b a c b d c 1d 1c 1e 1d 1f 1e 0 1f 1
  //   0 2 1 3 2 4 3 5 4 6 5 7 6 8 7 9 8 a 9 b a c b 1c 1b 1d 1c 1e 1d 1f 1e 0 1f 1 0 2 1 3 2 4 3 5 4 6 5 7
  //   6 8 7 9 8 a 9 b a 1b 1a 1c 1b 1d 1c 1e 1d 1f 1e 0 1f 1 0 2 1 3 2 4 3 5 4 6 5 7 6 8 7 9 8 a 9 1a 19
  //   1b 1a 1c 1b 1d 1c 1e 1d 1f 1e 0 1f 1 0 2 1 3 2 4 3 5 4 6 5 7 6 8 7 9 8 19 18 1a 19 1b 1a 1c 1b 1d 1c
  //   1e 1d 1f 1e 0 1f 1 0 2 1 3 2 4 3 5 4 6 5 7 6 8 7 18 17 19 18 1a 19 1b 1a 1c 1b 1d 1c 1e 1d 1f 1e 0
  //   1f 1 0 2 1 3 2 4 3 5 4 6 5 7 6 17 16 18 17 19 18 1a 19 1b 1a 1c 1b 1d 1c 1e 1d 1f 1e 0 1f 1 0 2 1 3
  //   2 4 3 5 4 6 5 16 15 17 16 18 17 19 18 1a 19 1b 1a 1c 1b 1d 1c 1e 1d 1f 1e 0 1f 1 0 2 1 3 2 4 3 5 4
  //   15 14 16 15 17 16 18 17 19 18 1a 19 1b 1a 1c 1b 1d 1c 1e 1d 1f 1e 0 1f 1 0 2 1 3 2 4 3 14 13 15 14
  //   16 15 17 16 18 17 19 18 1a 19 1b 1a 1c 1b 1d 1c 1e 1d 1f 1e 0 1f 1 0 2 1 3 2 13 12 14 13 15 14 16 15
  //   17 16 18 17 19 18 1a 19 1b 1a 1c 1b 1d 1c 1e 1d 1f 1e 0 1f 1 0 2 1 12 11 13 12 14 13 15 14 16 15 17
  //   16 18 17 19 18 1a 19 1b 1a 1c 1b 1d 1c 1e 1d 1f 1e 0 1f 1 0 11 10 12 11 13 12 14 13 15 14 16 15 17
  //   16 18 17 19 18 1a 19 1b 1a 1c 1b 1d 1c 1e 1d 1f 1e 0 1f 34*0 1 1 0 0 1 1 0 0 1 1 0 0 1 1 0 0 1 1 0 0
  //   1 1 0 0 1 1 0 0 1 1 4*0 4*2 4*0 4*2 4*0 4*2 4*0 4*2 0 0 1 1 2 2 3 3 0 0 1 1 2 2 3 3 0 0 1 1 2 2 3 3
  //   0 0 1 1 2 2 3 3 8*0 8*4 8*0 8*4 0 0 1 1 0 0 1 1 4 4 5 5 4 4 5 5 0 0 1 1 0 0 1 1 4 4 5 5 4 4 5 5 4*0
  //   4*2 4*4 4*6 4*0 4*2 4*4 4*6 0 0 1 1 2 2 3 3 4 4 5 5 6 6 7 7 0 0 1 1 2 2 3 3 4 4 5 5 6 6 7 7 16*0
  //   16*8 0 0 1 1 0 0 1 1 0 0 1 1 0 0 1 1 8 8 9 9 8 8 9 9 8 8 9 9 8 8 9 9 4*0 4*2 4*0 4*2 4*8 4*a 4*8 4*a
  //   0 0 1 1 2 2 3 3 0 0 1 1 2 2 3 3 8 8 9 9 a a b b 8 8 9 9 a a b b 8*0 8*4 8*8 8*c 0 0 1 1 0 0 1 1 4 4
  //   5 5 4 4 5 5 8 8 9 9 8 8 9 9 c c d d c c d d 4*0 4*2 4*4 4*6 4*8 4*a 4*c 4*e 0 0 1 1 2 2 3 3 4 4 5 5
  //   6 6 7 7 8 8 9 9 a a b b c c d d e e f f 0 0 1 1 2 2 3 3 4 4 5 5 6 6 7 7 8 8 9 9 a a b b c c d d e e
  //   f f 4*1 4*3 4*5 4*7 4*9 4*b 4*d 4*f 2 2 3 3 2 2 3 3 6 6 7 7 6 6 7 7 a a b b a a b b e e f f e e f f
  //   8*3 8*7 8*b 8*f 4 4 5 5 6 6 7 7 4 4 5 5 6 6 7 7 c c d d e e f f c c d d e e f f 4*5 4*7 4*5 4*7 4*d
  //   4*f 4*d 4*f 6 6 7 7 6 6 7 7 6 6 7 7 6 6 7 7 e e f f e e f f e e f f e e f f 16*7 16*f 8 8 9 9 a a b
  //   b c c d d e e f f 8 8 9 9 a a b b c c d d e e f f 4*9 4*b 4*d 4*f 4*9 4*b 4*d 4*f a a b b a a b b e
  //   e f f e e f f a a b b a a b b e e f f e e f f 8*b 8*f 8*b 8*f c c d d e e f f c c d d e e f f c c d
  //   d e e f f c c d d e e f f 4*d 4*f 4*d 4*f 4*d 4*f 4*d 4*f e e f f e e f f e e f f e e f f e e f f e
  //   e f f e e f f e e 34*f 0 0 1 1 2 2 3 3 4 4 5 5 6 6 7 7 8 8 9 9 a a b b c c d d e e f f 1 1 0 0 3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
  //   contents of ALUH (hex, n*v repeats v):
  //   0 1 1 2 2 3 3 4 4 5 5 6 6 7 7 8 8 9 9 a a b b c c d d e e f f 10 1 2 2 3 3 4 4 5 5 6 6 7 7 8 8 9 9 a
  //   a b b c c d d e e f f 10 10 11 2 3 3 4 4 5 5 6 6 7 7 8 8 9 9 a a b b c c d d e e f f 10 10 11 11 12
  //   3 4 4 5 5 6 6 7 7 8 8 9 9 a a b b c c d d e e f f 10 10 11 11 12 12 13 4 5 5 6 6 7 7 8 8 9 9 a a b b
  //   c c d d e e f f 10 10 11 11 12 12 13 13 14 5 6 6 7 7 8 8 9 9 a a b b c c d d e e f f 10 10 11 11 12
  //   12 13 13 14 14 15 6 7 7 8 8 9 9 a a b b c c d d e e f f 10 10 11 11 12 12 13 13 14 14 15 15 16 7 8 8
  //   9 9 a a b b c c d d e e f f 10 10 11 11 12 12 13 13 14 14 15 15 16 16 17 8 9 9 a a b b c c d d e e f
  //   f 10 10 11 11 12 12 13 13 14 14 15 15 16 16 17 17 18 9 a a b b c c d d e e f f 10 10 11 11 12 12 13
  //   13 14 14 15 15 16 16 17 17 18 18 19 a b b c c d d e e f f 10 10 11 11 12 12 13 13 14 14 15 15 16 16
  //   17 17 18 18 19 19 1a b c c d d e e f f 10 10 11 11 12 12 13 13 14 14 15 15 16 16 17 17 18 18 19 19
  //   1a 1a 1b c d d e e f f 10 10 11 11 12 12 13 13 14 14 15 15 16 16 17 17 18 18 19 19 1a 1a 1b 1b 1c d
  //   e e f f 10 10 11 11 12 12 13 13 14 14 15 15 16 16 17 17 18 18 19 19 1a 1a 1b 1b 1c 1c 1d e f f 10 10
  //   11 11 12 12 13 13 14 14 15 15 16 16 17 17 18 18 19 19 1a 1a 1b 1b 1c 1c 1d 1d 1e f 10 10 11 11 12 12
  //   13 13 14 14 15 15 16 16 17 17 18 18 19 19 1a 1a 1b 1b 1c 1c 1d 1d 1e 1e 1f 0 1f 1 0 2 1 3 2 4 3 5 4
  //   6 5 7 6 8 7 9 8 a 9 b a c b d c e d f e 1f 1e 0 1f 1 0 2 1 3 2 4 3 5 4 6 5 7 6 8 7 9 8 a 9 b a c b d
  //   c e d 1e 1d 1f 1e 0 1f 1 0 2 1 3 2 4 3 5 4 6 5 7 6 8 7 9 8 a 9 b a c b d c 1d 1c 1e 1d 1f 1e 0 1f 1
  //   0 2 1 3 2 4 3 5 4 6 5 7 6 8 7 9 8 a 9 b a c b 1c 1b 1d 1c 1e 1d 1f 1e 0 1f 1 0 2 1 3 2 4 3 5 4 6 5 7
  //   6 8 7 9 8 a 9 b a 1b 1a 1c 1b 1d 1c 1e 1d 1f 1e 0 1f 1 0 2 1 3 2 4 3 5 4 6 5 7 6 8 7 9 8 a 9 1a 19
  //   1b 1a 1c 1b 1d 1c 1e 1d 1f 1e 0 1f 1 0 2 1 3 2 4 3 5 4 6 5 7 6 8 7 9 8 19 18 1a 19 1b 1a 1c 1b 1d 1c
  //   1e 1d 1f 1e 0 1f 1 0 2 1 3 2 4 3 5 4 6 5 7 6 8 7 18 17 19 18 1a 19 1b 1a 1c 1b 1d 1c 1e 1d 1f 1e 0
  //   1f 1 0 2 1 3 2 4 3 5 4 6 5 7 6 17 16 18 17 19 18 1a 19 1b 1a 1c 1b 1d 1c 1e 1d 1f 1e 0 1f 1 0 2 1 3
  //   2 4 3 5 4 6 5 16 15 17 16 18 17 19 18 1a 19 1b 1a 1c 1b 1d 1c 1e 1d 1f 1e 0 1f 1 0 2 1 3 2 4 3 5 4
  //   15 14 16 15 17 16 18 17 19 18 1a 19 1b 1a 1c 1b 1d 1c 1e 1d 1f 1e 0 1f 1 0 2 1 3 2 4 3 14 13 15 14
  //   16 15 17 16 18 17 19 18 1a 19 1b 1a 1c 1b 1d 1c 1e 1d 1f 1e 0 1f 1 0 2 1 3 2 13 12 14 13 15 14 16 15
  //   17 16 18 17 19 18 1a 19 1b 1a 1c 1b 1d 1c 1e 1d 1f 1e 0 1f 1 0 2 1 12 11 13 12 14 13 15 14 16 15 17
  //   16 18 17 19 18 1a 19 1b 1a 1c 1b 1d 1c 1e 1d 1f 1e 0 1f 1 0 11 10 12 11 13 12 14 13 15 14 16 15 17
  //   16 18 17 19 18 1a 19 1b 1a 1c 1b 1d 1c 1e 1d 1f 1e 0 1f 34*0 1 1 0 0 1 1 0 0 1 1 0 0 1 1 0 0 1 1 0 0
  //   1 1 0 0 1 1 0 0 1 1 4*0 4*2 4*0 4*2 4*0 4*2 4*0 4*2 0 0 1 1 2 2 3 3 0 0 1 1 2 2 3 3 0 0 1 1 2 2 3 3
  //   0 0 1 1 2 2 3 3 8*0 8*4 8*0 8*4 0 0 1 1 0 0 1 1 4 4 5 5 4 4 5 5 0 0 1 1 0 0 1 1 4 4 5 5 4 4 5 5 4*0
  //   4*2 4*4 4*6 4*0 4*2 4*4 4*6 0 0 1 1 2 2 3 3 4 4 5 5 6 6 7 7 0 0 1 1 2 2 3 3 4 4 5 5 6 6 7 7 16*0
  //   16*8 0 0 1 1 0 0 1 1 0 0 1 1 0 0 1 1 8 8 9 9 8 8 9 9 8 8 9 9 8 8 9 9 4*0 4*2 4*0 4*2 4*8 4*a 4*8 4*a
  //   0 0 1 1 2 2 3 3 0 0 1 1 2 2 3 3 8 8 9 9 a a b b 8 8 9 9 a a b b 8*0 8*4 8*8 8*c 0 0 1 1 0 0 1 1 4 4
  //   5 5 4 4 5 5 8 8 9 9 8 8 9 9 c c d d c c d d 4*0 4*2 4*4 4*6 4*8 4*a 4*c 4*e 0 0 1 1 2 2 3 3 4 4 5 5
  //   6 6 7 7 8 8 9 9 a a b b c c d d e e f f 0 0 1 1 2 2 3 3 4 4 5 5 6 6 7 7 8 8 9 9 a a b b c c d d e e
  //   f f 4*1 4*3 4*5 4*7 4*9 4*b 4*d 4*f 2 2 3 3 2 2 3 3 6 6 7 7 6 6 7 7 a a b b a a b b e e f f e e f f
  //   8*3 8*7 8*b 8*f 4 4 5 5 6 6 7 7 4 4 5 5 6 6 7 7 c c d d e e f f c c d d e e f f 4*5 4*7 4*5 4*7 4*d
  //   4*f 4*d 4*f 6 6 7 7 6 6 7 7 6 6 7 7 6 6 7 7 e e f f e e f f e e f f e e f f 16*7 16*f 8 8 9 9 a a b
  //   b c c d d e e f f 8 8 9 9 a a b b c c d d e e f f 4*9 4*b 4*d 4*f 4*9 4*b 4*d 4*f a a b b a a b b e
  //   e f f e e f f a a b b a a b b e e f f e e f f 8*b 8*f 8*b 8*f c c d d e e f f c c d d e e f f c c d
  //   d e e f f c c d d e e f f 4*d 4*f 4*d 4*f 4*d 4*f 4*d 4*f e e f f e e f f e e f f e e f f e e f f e
  //   e f f e e f f e e 34*f 0 0 1 1 2 2 3 3 4 4 5 5 6 6 7 7 8 8 9 9 a a b b c c d d e e f f 1 1 0 0 3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
endmodule
